// Logisim project GLCPU.circ as structural Verilog
module alu (
  input  en,
  input  s0,
  input  s1,
  input  s3,
  input  c_in,
  input  a0,
  input  a1,
  input  a2,
  input  a3,
  input  a4,
  input  a5,
  input  a6,
  input  a7,
  input  b0,
  input  b1,
  input  b2,
  input  b3,
  input  b4,
  input  b5,
  input  b6,
  input  b7,
  output f0,
  output f1,
  output f2,
  output f3,
  output f4,
  output f5,
  output f6,
  output f7,
  output ovr,
  output c_out,
  output zero
);

  wire alu_op_select_op0, alu_op_select_op1, alu_op_select_op2, alu_op_select_op3, alu_op_select_op4,
       alu_slice0_c_out, alu_slice0_o, alu_slice1_c_out, alu_slice1_o, alu_slice2_c_out, alu_slice2_o,
       alu_slice3_c_out, alu_slice3_o, alu_slice4_c_out, alu_slice4_o, alu_slice5_c_out, alu_slice5_o,
       alu_slice6_c_out, alu_slice6_o, alu_slice7_o, and_1_out, and_3_out;

  alu_select alu_op_select (
    .s0(s0), .s1(s1), .s2(s3), .op0(alu_op_select_op0), .op1(alu_op_select_op1), .op2(alu_op_select_op2),
    .op3(alu_op_select_op3), .op4(alu_op_select_op4));
  alu_slice alu_slice0 (
    .op0(alu_op_select_op0), .op1(alu_op_select_op1), .op2(alu_op_select_op2), .op3(alu_op_select_op3),
    .op4(alu_op_select_op4), .a(a0), .b(b0), .c_in(c_in), .c_out(alu_slice0_c_out), .o(alu_slice0_o));
  alu_slice alu_slice1 (
    .op0(alu_op_select_op0), .op1(alu_op_select_op1), .op2(alu_op_select_op2), .op3(alu_op_select_op3),
    .op4(alu_op_select_op4), .a(a1), .b(b1), .c_in(alu_slice0_c_out), .c_out(alu_slice1_c_out),
    .o(alu_slice1_o));
  alu_slice alu_slice2 (
    .op0(alu_op_select_op0), .op1(alu_op_select_op1), .op2(alu_op_select_op2), .op3(alu_op_select_op3),
    .op4(alu_op_select_op4), .a(a2), .b(b2), .c_in(alu_slice1_c_out), .c_out(alu_slice2_c_out),
    .o(alu_slice2_o));
  alu_slice alu_slice3 (
    .op0(alu_op_select_op0), .op1(alu_op_select_op1), .op2(alu_op_select_op2), .op3(alu_op_select_op3),
    .op4(alu_op_select_op4), .a(a3), .b(b3), .c_in(alu_slice2_c_out), .c_out(alu_slice3_c_out),
    .o(alu_slice3_o));
  alu_slice alu_slice4 (
    .op0(alu_op_select_op0), .op1(alu_op_select_op1), .op2(alu_op_select_op2), .op3(alu_op_select_op3),
    .op4(alu_op_select_op4), .a(a4), .b(b4), .c_in(alu_slice3_c_out), .c_out(alu_slice4_c_out),
    .o(alu_slice4_o));
  alu_slice alu_slice5 (
    .op0(alu_op_select_op0), .op1(alu_op_select_op1), .op2(alu_op_select_op2), .op3(alu_op_select_op3),
    .op4(alu_op_select_op4), .a(a5), .b(b5), .c_in(alu_slice4_c_out), .c_out(alu_slice5_c_out),
    .o(alu_slice5_o));
  alu_slice alu_slice6 (
    .op0(alu_op_select_op0), .op1(alu_op_select_op1), .op2(alu_op_select_op2), .op3(alu_op_select_op3),
    .op4(alu_op_select_op4), .a(a6), .b(b6), .c_in(alu_slice5_c_out), .c_out(alu_slice6_c_out),
    .o(alu_slice6_o));
  alu_slice alu_slice7 (
    .op0(alu_op_select_op0), .op1(alu_op_select_op1), .op2(alu_op_select_op2), .op3(alu_op_select_op3),
    .op4(alu_op_select_op4), .a(a7), .b(b7), .c_in(alu_slice6_c_out), .c_out(c_out), .o(alu_slice7_o));
  xor xor_1 (ovr, alu_slice6_c_out, c_out);
  and and_1 (and_1_out, alu_slice7_o, alu_slice6_o, alu_slice5_o, alu_slice4_o);
  and and_2 (zero, and_1_out, and_3_out);
  and and_3 (and_3_out, alu_slice3_o, alu_slice2_o, alu_slice1_o, alu_slice0_o);
  assign f0 = en ? ~alu_slice0_o : 1'bz;  // Controlled_Inverter controlled_inverter_1
  assign f1 = en ? ~alu_slice1_o : 1'bz;  // Controlled_Inverter controlled_inverter_2
  assign f2 = en ? ~alu_slice2_o : 1'bz;  // Controlled_Inverter controlled_inverter_3
  assign f3 = en ? ~alu_slice3_o : 1'bz;  // Controlled_Inverter controlled_inverter_4
  assign f4 = en ? ~alu_slice4_o : 1'bz;  // Controlled_Inverter controlled_inverter_5
  assign f5 = en ? ~alu_slice5_o : 1'bz;  // Controlled_Inverter controlled_inverter_6
  assign f6 = en ? ~alu_slice6_o : 1'bz;  // Controlled_Inverter controlled_inverter_7
  assign f7 = en ? ~alu_slice7_o : 1'bz;  // Controlled_Inverter controlled_inverter_8
endmodule

module alu_select (
  input  s0,
  input  s1,
  input  s2,
  output op0,
  output op1,
  output op2,
  output op3,
  output op4
);

  wire nand_1_out, not_1_out;

  xor xor_1 (op0, s0, s2);
  xor xor_2 (op1, s1, s2);
  not not_1 (not_1_out, s2);
  nand nand_1 (nand_1_out, s0, s1, not_1_out);
  nand nand_2 (op2, nand_1_out, not_1_out);
  not not_2 (op3, nand_1_out);
  nor nor_1 (op4, not_1_out, s1);
endmodule

module alu_slice (
  input  op0,
  input  op1,
  input  op2,
  input  op3,
  input  op4,
  input  a,
  input  b,
  input  c_in,
  output c_out,
  output o
);

  wire nand_1_out, nand_2_out, nor_1_out, nor_2_out, nor_3_out, nor_4_out, not_1_out, xor_1_out, xor_2_out,
       xor_3_out;

  xor xor_1 (xor_1_out, op0, a);
  xor xor_2 (xor_2_out, op1, b);
  nand nand_1 (nand_1_out, xor_1_out, xor_2_out);
  nor nor_1 (nor_1_out, xor_1_out, xor_2_out);
  not not_1 (not_1_out, nor_1_out);
  nor nor_2 (nor_2_out, nand_1_out, op4);
  nor nor_3 (nor_3_out, nor_1_out, op3);
  nor nor_4 (nor_4_out, c_in, op2);
  nand nand_2 (nand_2_out, not_1_out, c_in);
  xor xor_3 (xor_3_out, nor_2_out, nor_3_out);
  nand nand_3 (c_out, nand_1_out, nand_2_out);
  xor xor_4 (o, xor_3_out, nor_4_out);
endmodule

module flags_register (
  input  ovrIn,
  input  cIn,
  input  zIn,
  input  store,
  input  clk,
  input  n_rst,
  output overOut,
  output cOut,
  output zOut
);

  wire not_1_out;

  not not_1 (not_1_out, n_rst);
  Register #(.width(1)) register_1 (.D(ovrIn), .en(store), .clk(clk), .Q(overOut), .clr(not_1_out));
  Register #(.width(1)) register_2 (.D(cIn), .en(store), .clk(clk), .Q(cOut), .clr(not_1_out));
  Register #(.width(1)) register_3 (.D(zIn), .en(store), .clk(clk), .Q(zOut), .clr(not_1_out));
endmodule

module cpu (
  input  clk,
  input  n_rst
);

  wire alu_1_c_out, alu_1_ovr, alu_1_zero;

  alu alu_1 (
    .ovr(alu_1_ovr), .c_out(alu_1_c_out), .zero(alu_1_zero));  // open: en, s0, s1, s3, c_in, a0, a1, a2, a3, a4, a5, a6, a7, b0, b1, b2, b3, b4, b5, b6, b7, f0, f1, f2, f3, f4, f5, f6, f7
  flags_register flags_register_1 (
    .ovrIn(alu_1_ovr), .cIn(alu_1_c_out), .zIn(alu_1_zero));  // open: store, clk, n_rst, overOut, cOut, zOut
endmodule

module address_register_control (
  input  clk,
  input  n_rst,
  input  pcInc,
  input  pcLoad,
  input  arInc,
  input  arLoad,
  input  sel,
  input  [7:0] data,
  input  tlLoad,
  input  thLoad,
  output [15:0] programCounter,
  output [15:0] addressRegister
);

  wire [15:0] multiplexer_1_out, t_1_abus;

  Multiplexer #(.width(16)) multiplexer_1 (.in0(programCounter), .in1(t_1_abus), .out(multiplexer_1_out), .sel(sel));
  t t_1 (.clk(clk), .data(data), .tlLoad(tlLoad), .thLoad(thLoad), .aBus(t_1_abus));
  pc pcReg (
    .clk(clk), .n_rst(n_rst), .pcInc(pcInc), .pcLoad(pcLoad), .aBus(multiplexer_1_out),
    .programCounter(programCounter));
  ar aReg (
    .clk(clk), .n_rst(n_rst), .arInc(arInc), .arLoad(arLoad), .aBus(multiplexer_1_out),
    .addressRegister(addressRegister));
endmodule

module pc (
  input  clk,
  input  n_rst,
  input  pcInc,
  input  pcLoad,
  input  [15:0] aBus,
  output [15:0] programCounter
);

  wire not_1_out, or_1_out;
  wire [15:0] adder_1_out, multiplexer_1_out;

  not not_1 (not_1_out, n_rst);
  or or_1 (or_1_out, pcInc, pcLoad);
  Multiplexer #(.width(16)) multiplexer_1 (.in0(adder_1_out), .in1(aBus), .out(multiplexer_1_out), .sel(pcLoad));
  Register #(.width(16)) pcReg (.D(multiplexer_1_out), .en(or_1_out), .clk(clk), .Q(programCounter), .clr(not_1_out));
  Adder #(.width(16)) adder_1 (.a(programCounter), .b({{15{1'b0}}, pcInc}), .out(adder_1_out));  // open: cin, cout
endmodule

module t (
  input  clk,
  input  [7:0] data,
  input  tlLoad,
  input  thLoad,
  output [15:0] aBus
);

  Register tl (.D(data), .en(tlLoad), .clk(clk), .Q(aBus[7:0]));  // open: clr
  Register th (.D(data), .en(thLoad), .clk(clk), .Q(aBus[15:8]));  // open: clr
endmodule

module ar (
  input  clk,
  input  n_rst,
  input  arInc,
  input  arLoad,
  input  [15:0] aBus,
  output [15:0] addressRegister
);

  wire not_1_out, or_1_out;
  wire [15:0] adder_1_out, multiplexer_1_out;

  not not_1 (not_1_out, n_rst);
  or or_1 (or_1_out, arInc, arLoad);
  Multiplexer #(.width(16)) multiplexer_1 (.in0(adder_1_out), .in1(aBus), .out(multiplexer_1_out), .sel(arLoad));
  Register #(.width(16)) arReg (.D(multiplexer_1_out), .en(or_1_out), .clk(clk), .Q(addressRegister), .clr(not_1_out));
  Adder #(.width(16)) adder_1 (.a(addressRegister), .b({{15{1'b0}}, arInc}), .out(adder_1_out));  // open: cin, cout
endmodule
